# Fritzing sketch dispenser (saved by Fritzing 0.9.3b)
circuit board: 8.46667cm x 5.64444cm
breadboards: 1

parts:
  Q1 = NPN-Transistor [part_number=PN2222 package="TO92 [THT]"]
  R1 = Resistor [tolerance=±5% resistance=330 package=THT]
  Part1 = Arduino Uno (Rev3)
  J1 = Infrared Proximity Sensor [part_number=GP2Y0A41SK0F]
  LED1 = RGB LED (com. cathode, rgb) [part_number="100F5T-YT-RGB-CC " package="5 mm [THT]"]
  R2 = Resistor [tolerance=±1% resistance=100 package="0805 [SMD]"]
  M1 = DC Motor [part_number=LYSB01IUVHB8E-ELECTRNCS]
  VCC4 = Battery
  VCC1 = Battery
  VCC2 = Battery
  VCC3 = Battery
  D1 = Rectifier Diode [breakdown_voltage=3.6V part_number=1N4001 package="300 mil [THT]"]

nets:
  N1: Q1.E, M1.pin_2
  N2: Q1.B, R1.Pin_1
  GND: Q1.C, Part1.GND, J1.GND, R2.Pin_0, VCC4.-, D1.anode
  N3: R1.Pin_0, Part1.D10_PWM/SS
  N4: Part1.A0, J1.Vout
  N5: Part1.D11_PWM/MOSI, LED1.red_anode
  N6: Part1.D5_PWM, LED1.blue_anode
  N7: Part1.D6_PWM, LED1.green_anode
  5V: Part1.5V, J1.Vcc
  N8: Part1.VIN, M1.pin_1, VCC1.+, D1.cathode
  N9: LED1.common_cathode, R2.Pin_1
  N10: VCC4.+, VCC3.-
  N11: VCC1.-, VCC2.+
  N12: VCC2.-, VCC3.+
